// Logisim project vending_machine.circ as structural Verilog: 1 circuit, main circuit main
module main (
  output CHO,
  output CHG,
  output S10p,
  output S5p
);

  wire and_1_out, and_2_out, and_3_out, and_5_out, and_6_out, and_7_out, and_8_out, and_9_out, clock_1_out,
       clock_2_out, d_ff_1_q, d_ff_2_q, not_1_out, not_2_out, not_3_out, not_4_out, not_5_out, not_6_out,
       not_7_out, not_8_out, xnor_1_out;

  Clock clock_1 (.out(clock_1_out));
  Clock clock_2 (.out(clock_2_out));
  xnor xnor_1 (xnor_1_out, clock_2_out, clock_1_out);
  D_Flip_Flop d_ff_1 (.clk(xnor_1_out), .D(S10p), .Q(d_ff_1_q));  // open: Qn, preset, en, reset
  D_Flip_Flop d_ff_2 (.clk(xnor_1_out), .D(S5p), .Q(d_ff_2_q));  // open: Qn, preset, en, reset
  not not_1 (not_1_out, d_ff_1_q);
  not not_2 (not_2_out, d_ff_2_q);
  not not_3 (not_3_out, clock_1_out);
  not not_4 (not_4_out, clock_2_out);
  not not_5 (not_5_out, d_ff_1_q);
  not not_6 (not_6_out, d_ff_2_q);
  not not_7 (not_7_out, clock_1_out);
  not not_8 (not_8_out, clock_2_out);
  and and_1 (and_1_out, d_ff_2_q, clock_1_out);
  or or_1 (CHO, and_1_out, and_2_out, and_3_out);
  and and_2 (and_2_out, d_ff_1_q, clock_2_out);
  and and_3 (and_3_out, d_ff_1_q, clock_1_out);
  and and_4 (CHG, d_ff_1_q, clock_1_out);
  and and_5 (and_5_out, not_1_out, not_2_out, clock_1_out);
  and and_6 (and_6_out, d_ff_2_q, clock_2_out);
  and and_7 (and_7_out, d_ff_1_q, not_3_out, not_4_out);
  and and_8 (and_8_out, not_5_out, not_6_out, clock_2_out);
  and and_9 (and_9_out, d_ff_2_q, not_7_out, not_8_out);
  or or_2 (S10p, and_5_out, and_6_out, and_7_out);
  or or_3 (S5p, and_8_out, and_9_out);

  // Notes on the sheet:
  //   10p
  //   5p
endmodule
